# Fritzing sketch cablage (saved by Fritzing 1.0.1rc)
# 18650 Li-ion Battery: CC-BY Dr Kristofer Chan, King's College London/Remote-research.org

parts:
  J1 = Basic Servo
  M1 = DC Motor [voltage_(max)=6V voltage_(min)=3V]
  Composant1 = Arduino Nano (Rev3.0) (ICSP)
  U1 = Voltage Regulator [package=to220-adj]
  J2 = Camdenboss CTB0158-4 [part_number=CTB0158-4 package=THT]
  J3 = female pin header, 4 pins [form="♀ (female)"]
  J4 = female pin header, 4 pins [form="♀ (female)"]
  CPU1 = p1
  BAT1 = 18650 Li-ion Battery [package=battery-18650]
  BAT2 = 18650 Li-ion Battery [package=battery-18650]
  C1 = Capacitor Polarized [package=cpol-radial-1000uf-25v]

nets:
  GND: J1.gnd, Composant1.GND, U1.IN, J2.terminal_4, J4.pin1, CPU1.connector15, BAT1.-, C1.-
  VCC: J1.vcc, Composant1.VIN, U1.OUT, J3.pin1, CPU1.connector16, C1.+
  N1: M1.pin_1, J2.terminal_1
  N2: M1.pin_2, J2.terminal_2
  N3: Composant1.D5, J3.pin4
  N4: Composant1.D6, J4.pin4
  N5: U1.ADJ, J2.terminal_3, BAT2.+
  N6: BAT1.+, BAT2.-

notes:
  7805
  2x 18650 lithium ions
  Moteur de traction
  controle moteur
  IBT2
  Arduino nano
  Servomoteur de direction
  condo 4000uf
  ESP 32 Wroom 30 pins

custom parts:
  18650 Li-ion Battery: 18650 li-ion Battery Standard 18650 battery with interactive connectors Creative Common Attribution 4.0 International (CC-BY 4.0) license. Any use of this part requires attribution of Dr Kristofer Chan, Department of Geography, King's College London. Contact kristofer.chan [at] kcl.ac.uk OR kris [at] remote-research.org for further information.
