# Fritzing sketch Untitled Sketch (saved by Fritzing 1.0.1rc)

parts:
  J1 = Basic Servo  # not connected
  M1 = DC Motor [voltage_(max)=6V voltage_(min)=3V]
  Composant1 = Arduino Nano (Rev3.0) (ICSP)
  VCC1 = Battery
  U1 = Voltage Regulator [package=to220-adj]
  J2 = Camdenboss CTB0158-4 [part_number=CTB0158-4 package=THT]
  J3 = female pin header, 4 pins [form="♀ (female)"]
  J4 = female pin header, 4 pins [form="♀ (female)"]

nets:
  N1: M1.pin_1, J2.terminal_1
  N2: M1.pin_2, J2.terminal_2
  N3: Composant1.D5, J3.pin4
  N4: Composant1.D6, J4.pin4
  N5: VCC1.-, U1.IN, J2.terminal_4, J4.pin1
  N6: VCC1.+, U1.ADJ, J2.terminal_3
  N7: U1.OUT, J3.pin1

notes:
  7805
